# Fritzing sketch Battery_Drop_Control_Connections (saved by Fritzing 0.9.4)
breadboards: 1

parts:
  Componente1 = Adafruit Motor/Stepper/Servo Shield [part_number="Adafruit #1438"]
  D1 = Diode [package=diode-hv]
  WeMos_D1_R1 = WeMos D1 R2
  SERVO1 = Tower Pro SG90 servo [part_number=101246]
  U1 = LIPO-110mAh [package=lipo-110]
  R1 = Resistor [tolerance=±5% resistance=220k package=THT]
  J4 = Power Jack [package=power_jack_smd]
  JACK1 = 2.1mm Barrel Jack with Terminal Block
  U3 = SWITCH-SPST-2 [package=r_sw_th]
  R5 = TRIMPOT [package=3362u-2]
  LED1 = smd LED [color="Red (633nm)" package="0805 [SMD]"]
  J1 = Infrared Proximity Sensor

nets:
  N1: Componente1.AD0, J1.Vout
  N2: Componente1.D3, Componente1.D11, WeMos_D1_R1.D3
  N3: Componente1.D5, Componente1.D6, WeMos_D1_R1.(D5)
  GND: Componente1.GND, WeMos_D1_R1.GND, SERVO1.GND, LED1.cathode, J1.GND
  N4: Componente1.+5V, D1.A
  N5: Componente1.D12, Componente1.D10, WeMos_D1_R1.D10
  5V: Componente1.VMOTOR, D1.C, WeMos_D1_R1.5V, SERVO1.+5V, J1.Vcc
  +3V3: Componente1.+3V3, WeMos_D1_R1.3.3V
  N6: Componente1.D0, WeMos_D1_R1.D0/RX
  N7: Componente1.D1, WeMos_D1_R1.D1/TX
  N8: Componente1.D4, WeMos_D1_R1.D4
  N9: Componente1.D7, WeMos_D1_R1.(D7)
  N10: Componente1.D8, WeMos_D1_R1.D8
  N11: Componente1.D13, WeMos_D1_R1.D13
  N12: Componente1./RST, WeMos_D1_R1.RESET
  VIN: Componente1.VIN, WeMos_D1_R1.VIN
  N13: WeMos_D1_R1.D2, LED1.anode
  N14: WeMos_D1_R1.(D6), R1.Pin_1, R5.CCW
  N15: WeMos_D1_R1.D9, SERVO1.Signal
  N16: U1.+, J4.GNDBREAK, U3.O
  N17: U1.-, J4.GND, JACK1.NEG, R5.CW
  N18: R1.Pin_0, JACK1.POS, U3.P

custom parts:
  Adafruit Motor/Stepper/Servo Shield: The original Adafruit Motorshield kit is one of our most beloved kits, which is why we decided to make something even better. We have upgraded the shield kit to make the bestest, easiest way to drive DC and Stepper motors. This shield will make quick work of your next robotics project! We kept the ability to drive up to 4 DC motors or 2 stepper motors, but added many improvements: Instead of a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
  WeMos D1 R2: The D1 R2 is a mini wifi board based on the ESP-8266EX.
  Tower Pro SG90 servo: Original file by John De Cristofaro http://www.adafruit.com/products/1449 Adafruit Feedback Servo (Small) Edited by: e-radionica.com 28/9/2015
