# Fritzing sketch Components_1 (saved by Fritzing 0.9.4)
breadboards: 1

parts:
  J1 = Infrared Proximity Sensor
  SERVO1 = Tower Pro SG90 servo [part_number=101246]  # not connected
  MOTOR1 = 28BYJ-48 Stepper Motor
  MOTOR2 = 28BYJ-48 Stepper Motor
  Componente1 = Adafruit Motor/Stepper/Servo Shield [part_number="Adafruit #1438"]
  D1 = Diode [package=diode-hv]
  WeMos_D1_R1 = WeMos D1 R2

nets:
  N1: J1.Vout, Componente1.AD0, WeMos_D1_R1.A0
  GND: J1.GND, MOTOR1.YELLOW, MOTOR2.YELLOW, Componente1.GND, WeMos_D1_R1.GND
  VCC: J1.Vcc, WeMos_D1_R1.5V
  N2: MOTOR1.RED, Componente1.M1A
  N3: MOTOR1.ORANGE, Componente1.M1B
  N4: MOTOR1.PINK, Componente1.M2B
  N5: MOTOR1.BLUE, Componente1.M2A
  N6: MOTOR2.RED, Componente1.M3A
  N7: MOTOR2.ORANGE, Componente1.M3B
  N8: MOTOR2.PINK, Componente1.M4B
  N9: MOTOR2.BLUE, Componente1.M4A
  N10: Componente1.+5V, D1.A
  N11: Componente1.VMOTOR, D1.C
  +3V3: Componente1.+3V3, WeMos_D1_R1.3.3V
  N12: Componente1.D0, WeMos_D1_R1.D0/RX
  N13: Componente1.D1, WeMos_D1_R1.D1/TX
  N14: Componente1.D3, WeMos_D1_R1.D3
  N15: Componente1.D4, WeMos_D1_R1.D4
  N16: Componente1.D5, WeMos_D1_R1.(D5)
  N17: Componente1.D7, WeMos_D1_R1.(D7)
  N18: Componente1.D8, WeMos_D1_R1.D8
  N19: Componente1.D10, WeMos_D1_R1.D10
  N20: Componente1.D13, WeMos_D1_R1.D13
  N21: Componente1./RST, WeMos_D1_R1.RESET

custom parts:
  Tower Pro SG90 servo: Original file by John De Cristofaro http://www.adafruit.com/products/1449 Adafruit Feedback Servo (Small) Edited by: e-radionica.com 28/9/2015
  Adafruit Motor/Stepper/Servo Shield: The original Adafruit Motorshield kit is one of our most beloved kits, which is why we decided to make something even better. We have upgraded the shield kit to make the bestest, easiest way to drive DC and Stepper motors. This shield will make quick work of your next robotics project! We kept the ability to drive up to 4 DC motors or 2 stepper motors, but added many improvements: Instead of a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
  WeMos D1 R2: The D1 R2 is a mini wifi board based on the ESP-8266EX.
