# Fritzing sketch Steppers_to_Shield (saved by Fritzing 0.9.4)

parts:
  Componente1 = Adafruit Motor/Stepper/Servo Shield [part_number="Adafruit #1438"]
  MOTOR1 = 28BYJ-48 Stepper Motor
  MOTOR2 = 28BYJ-48 Stepper Motor

nets:
  N1: Componente1.M2A, MOTOR2.BLUE
  N2: Componente1.M2B, MOTOR2.RED
  N3: Componente1.GND, MOTOR1.YELLOW, MOTOR2.YELLOW
  N4: Componente1.M1B, MOTOR2.ORANGE
  N5: Componente1.M1A, MOTOR2.PINK
  N6: Componente1.M3A, MOTOR1.BLUE
  N7: Componente1.M3B, MOTOR1.RED
  N8: Componente1.M4B, MOTOR1.ORANGE
  N9: Componente1.M4A, MOTOR1.PINK

custom parts:
  Adafruit Motor/Stepper/Servo Shield: The original Adafruit Motorshield kit is one of our most beloved kits, which is why we decided to make something even better. We have upgraded the shield kit to make the bestest, easiest way to drive DC and Stepper motors. This shield will make quick work of your next robotics project! We kept the ability to drive up to 4 DC motors or 2 stepper motors, but added many improvements: Instead of a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
