# Fritzing sketch UltrasonicSensorConnections (saved by Fritzing 0.9.4)
breadboards: 1

parts:
  Componente1 = Adafruit Motor/Stepper/Servo Shield [part_number="Adafruit #1438"]
  D1 = Diode [package=diode-hv]
  WeMos_D1_R1 = WeMos D1 R2
  HC-SR04_Sensor_1 = HC-SR04 Ultrasonic Distance Sensor
  SERVO2 = Tower Pro SG90 servo [part_number=101246]

nets:
  N1: Componente1.D3, Componente1.D11, WeMos_D1_R1.D3
  N2: Componente1.D5, Componente1.D6, WeMos_D1_R1.(D5)
  GND: Componente1.GND, WeMos_D1_R1.GND, HC-SR04_Sensor_1.GND, SERVO2.GND
  N3: Componente1.+5V, D1.A
  N4: Componente1.D12, Componente1.D10, WeMos_D1_R1.D10
  5V: Componente1.VMOTOR, D1.C, WeMos_D1_R1.5V, HC-SR04_Sensor_1.VCC, SERVO2.+5V
  +3V3: Componente1.+3V3, WeMos_D1_R1.3.3V
  N5: Componente1.D0, WeMos_D1_R1.D0/RX
  N6: Componente1.D1, WeMos_D1_R1.D1/TX
  N7: Componente1.D4, WeMos_D1_R1.D4
  N8: Componente1.D7, WeMos_D1_R1.(D7)
  N9: Componente1.D8, WeMos_D1_R1.D8
  N10: Componente1.D13, WeMos_D1_R1.D13
  N11: Componente1./RST, WeMos_D1_R1.RESET
  VIN: Componente1.VIN, WeMos_D1_R1.VIN
  N12: WeMos_D1_R1.D2, HC-SR04_Sensor_1.TRIG
  N13: WeMos_D1_R1.(D6), HC-SR04_Sensor_1.ECHO
  N14: WeMos_D1_R1.D9, SERVO2.Signal

custom parts:
  Adafruit Motor/Stepper/Servo Shield: The original Adafruit Motorshield kit is one of our most beloved kits, which is why we decided to make something even better. We have upgraded the shield kit to make the bestest, easiest way to drive DC and Stepper motors. This shield will make quick work of your next robotics project! We kept the ability to drive up to 4 DC motors or 2 stepper motors, but added many improvements: Instead of a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
  WeMos D1 R2: The D1 R2 is a mini wifi board based on the ESP-8266EX.
  Tower Pro SG90 servo: Original file by John De Cristofaro http://www.adafruit.com/products/1449 Adafruit Feedback Servo (Small) Edited by: e-radionica.com 28/9/2015
